# Fritzing sketch Robot Schematic (saved by Fritzing 0.9.3b)

parts:
  L298N2 = L298N DC motor driver
  U1 = STM32F303 [package=LQFP-48]
  M1 = gy9250
  M2 = DC Motor
  U2 = LIPO-1000mAh [package=lipo-1000]

nets:
  N1: L298N2.OUT1, M2.pin_2
  N2: L298N2.OUT2, M2.pin_1
  N3: L298N2.12V, U2.+
  GND: L298N2.GND, U1.GND, M1.pin2, U2.-
  5V: L298N2.5V, U1.5V
  N4: L298N2.IN1, U1.A0
  N5: L298N2.IN2, U1.A1
  N6: U1.B7, M1.pin3
  N7: U1.B8, M1.pin4
  N8: U1.3V3, M1.pin1

custom parts:
  L298N DC motor driver: 2x DC motor driver with 78M05 positive voltage regulator (7..35 V) L298N: max 46 V, 2 A Set 5 V Enable jumper to enable 5 V regultor (needed for the L298N) and +5 V output at screw terminal or supply external +5 V at screw terminal Set ENA and/or ENB to +5 V to enable motor permanently or supply ENA and/or ENB with PWM signal IN1 and IN2 set rotation directory for motor A (OUT1/OUT2) IN2 and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
  STM32F303: Medium density Cortex-M3 microcontroller.
  gy9250: MPU-9250 module (three-axis gyroscope + three-axis acceleration + three-axis magnetic field). The generic model from ebay et. al. rather than the Sparkfun version.
